// Logisim project lil_CPU.circ as structural Verilog: 13 circuits, main circuit main
module main (
  input  [15:0] in_1,
  input  [15:0] in_2,
  input  in_3
);

  wire clock_1_out, cpu_1_p3, cpu_1_p4;
  wire [15:0] cpu_1_p5, cpu_1_p8, cpu_1_p9, ram_1_dout;
  wire [16:0] cpu_1_p7;
  wire [31:0] cpu_1_p6;

  Clock clock_1 (.out(clock_1_out));
  // Probe on in_1
  // Probe on in_2
  // CPU cpu_1: pin names not known; wires that end beside it: clock_1_out, in_3, cpu_1_p3, cpu_1_p4, cpu_1_p5, cpu_1_p6, cpu_1_p7, cpu_1_p8, cpu_1_p9, in_3, clock_1_out
  // Probe on cpu_1_p7
  RAM #(.addrWidth(17), .clearpin("true"), .dataWidth(16), .enables("line")) ram_1 (
    .addr(cpu_1_p7), .we(cpu_1_p4), .clk(clock_1_out), .din(cpu_1_p8), .dout(ram_1_dout), .clr(in_3));
  // Probe on cpu_1_p8
  Pull_Resistor pull_resistor_1 (.node(cpu_1_p9));
  assign cpu_1_p9 = cpu_1_p3 ? ram_1_dout : 16'bz;  // Controlled_Buffer controlled_buffer_1
  ROM #(.addrWidth(16), .dataWidth(32)) rom_1 (.addr(cpu_1_p5), .data(cpu_1_p6));

  // Notes on the sheet:
  //   contents of rom_1 (hex, n*v repeats v):
  //   1808150 20808123 20808123 20808123
endmodule

module CPU (
  input  [15:0] Main_Bus_In,
  input  RESET,
  input  CLK,
  input  [31:0] Instruction_Set,
  input  [2:0] in_5,
  input  in_6,
  input  [2:0] in_7,
  input  in_8,
  input  [2:0] in_9,
  input  in_10,
  output [15:0] Main_Bus_Out,
  output [16:0] Adress_Bus_Out,
  output Write_Data_to_Memory,
  output Read_Data_from_Memory,
  output READ_IO,
  output Write_IO,
  output [15:0] Instruction_Pointer,
  output [2:0] out_18,
  output [2:0] out_19
);

  wire instruction_decoder_1_cache_select, instruction_decoder_1_reg_enable,
       instruction_decoder_1_reg_out_enable, instruction_decoder_1_reg_out_to_mainbus_select,
       instruction_decoder_1_word_select;
  wire [1:0] instruction_decoder_1_register_in_select;
  wire [2:0] instruction_decoder_1_reg_out_select, instruction_decoder_1_reg_select;
  wire [15:0] alu_1_to_internal_bus, general_purpose_registers_1_to_internal_data_bus,
       general_purpose_registers_1_to_main_bus, or_2_out, relocation_registers_1_to_internal_data_bus,
       relocation_registers_1_to_main_bus;

  assign Main_Bus_Out = relocation_registers_1_to_main_bus | general_purpose_registers_1_to_main_bus;  // OR_Gate or_1, 16 bits wide
  assign out_18 = in_6 ? in_5 : 3'bz;  // Controlled_Buffer controlled_buffer_1
  General_Purpose_Registers general_purpose_registers_1 (
    .To_Internal_Data_Bus(general_purpose_registers_1_to_internal_data_bus),
    .To_Main_Bus(general_purpose_registers_1_to_main_bus), .From_Main_Bus(Main_Bus_In),
    .From_Internal_Data_Bus(or_2_out), .Instruction_Set(Instruction_Set), .Reset(RESET), .CLK(CLK));
  assign or_2_out = relocation_registers_1_to_internal_data_bus | alu_1_to_internal_bus;  // OR_Gate or_2, 16 bits wide
  ALU alu_1 (
    .To_Internal_Bus(alu_1_to_internal_bus), .Instruction_Set(Instruction_Set),
    .From_Internal_Bus(general_purpose_registers_1_to_internal_data_bus), .CLK(CLK));
  assign out_18 = in_8 ? in_7 : 3'bz;  // Controlled_Buffer controlled_buffer_2
  Relocation_Registers relocation_registers_1 (
    .out_13(Instruction_Pointer), .To_Internal_Data_Bus(relocation_registers_1_to_internal_data_bus),
    .To_Main_Bus(relocation_registers_1_to_main_bus), .To_Adress_Bus(Adress_Bus_Out[15:0]), .CLK(CLK),
    .RESET(RESET), .Word_Select(instruction_decoder_1_word_select),
    .REG_Enable(instruction_decoder_1_reg_enable), .REG_Select(instruction_decoder_1_reg_select),
    .Register_in_Select(instruction_decoder_1_register_in_select),
    .Reg_Out_Select(instruction_decoder_1_reg_out_select),
    .Reg_Out_Enable(instruction_decoder_1_reg_out_enable), .Cache_Select(instruction_decoder_1_cache_select),
    .REG_Out_to_Mainbus_Select(instruction_decoder_1_reg_out_to_mainbus_select), .From_Main_Bus(Main_Bus_In),
    .From_Internal_Data_Bus(general_purpose_registers_1_to_internal_data_bus));
  Pull_Resistor pull_resistor_1 (.node(out_18));
  Instruction_Decoder instruction_decoder_1 (
    .REG_Enable(instruction_decoder_1_reg_enable), .REG_Select(instruction_decoder_1_reg_select),
    .Register_in_Select(instruction_decoder_1_register_in_select),
    .Reg_Out_Enable(instruction_decoder_1_reg_out_enable), .Read_Data_from_Memory(Read_Data_from_Memory),
    .Reg_Out_Select(instruction_decoder_1_reg_out_select), .Cache_Select(instruction_decoder_1_cache_select),
    .REG_Out_to_Mainbus_Select(instruction_decoder_1_reg_out_to_mainbus_select),
    .Write_Data_to_Memory(Write_Data_to_Memory), .Use_Cache(Adress_Bus_Out[16]),
    .Word_Select(instruction_decoder_1_word_select), .Instruction_Set(Instruction_Set));
  assign out_18 = in_10 ? in_9 : 3'bz;  // Controlled_Buffer controlled_buffer_3

  assign out_19 = out_18;
endmodule

module Bus_Interface_Unit (
  input  [15:0] Main_Bus_In,
  output Read_Data_from_Memory,
  output Write_Data_to_Memory,
  output READ_IO,
  output Write_IO,
  output Instruction_Fetch,
  output [15:0] Main_Bus_Out
);
endmodule

module Relocation_Registers (
  input  CLK,
  input  RESET,
  input  [15:0] From_Main_Bus,
  input  [15:0] From_Internal_Data_Bus,
  input  Word_Select,
  input  REG_Enable,
  input  [2:0] REG_Select,
  input  [1:0] Register_in_Select,
  input  [2:0] Reg_Out_Select,
  input  Reg_Out_Enable,
  input  Cache_Select,
  input  REG_Out_to_Mainbus_Select,
  output [15:0] out_13,
  output [15:0] To_Internal_Data_Bus,
  output [15:0] To_Main_Bus,
  output [15:0] To_Adress_Bus
);

  wire and_1_out, and_2_out, comparator_1_gt, decoder_1_out4, decoder_1_out5, decoder_1_out6, not_1_out,
       one_bit_narrow_or_1_o, undriven, undriven_2;
  wire [15:0] Base_Pointer_q, multiplexer_1_out, multiplexer_3_out, pull_resistor_1_node,
       stack_pointer_1_data_out, undriven_3;

  Decoder #(.select(3)) decoder_1 (
    .out4(decoder_1_out4), .out5(decoder_1_out5), .out6(decoder_1_out6), .sel(REG_Select), .en(and_1_out));  // open: out0, out1, out2, out3, out7
  and and_1 (and_1_out, Word_Select, REG_Enable);
  not not_1 (not_1_out, undriven_2);
  One_Bit_Narrow_OR one_bit_narrow_or_1 (.O(one_bit_narrow_or_1_o), .A(undriven_2), .B(undriven));
  and and_2 (and_2_out, Word_Select, Reg_Out_Enable);
  Counter #(.max('hffff), .trigger("falling"), .width(16)) Instruction_Pointer (
    .load(decoder_1_out6), .D(multiplexer_1_out), .Q(out_13), .clk(CLK), .clr(RESET));  // open: count, carry, up
  Stack_Pointer stack_pointer_1 (
    .Data_OUT(stack_pointer_1_data_out), .Load_Data(decoder_1_out4), .Data_IN(multiplexer_1_out),
    .Enable(one_bit_narrow_or_1_o), .CLK(CLK), .Up_Down(not_1_out), .RESET(RESET), .POP(undriven_2));
  Register #(.width(16)) Base_Pointer (
    .D(multiplexer_1_out), .en(decoder_1_out5), .Q(Base_Pointer_q), .clk(CLK), .clr(RESET));
  Multiplexer #(.enable("false"), .select(2), .width(16)) multiplexer_1 (
    .in0(undriven_3), .in1(From_Internal_Data_Bus), .in2(From_Main_Bus), .out(multiplexer_1_out),
    .sel(Register_in_Select));  // open: in3
  Comparator #(.mode("unsigned"), .width(16)) comparator_1 (
    .a(undriven_3), .b({16{1'b0}}), .gt(comparator_1_gt));  // open: eq, lt
  Pull_Resistor pull_resistor_1 (.node(pull_resistor_1_node));
  Multiplexer #(.select(3), .width(16)) multiplexer_2 (
    .in4(stack_pointer_1_data_out), .in5(Base_Pointer_q), .in6(out_13), .out(pull_resistor_1_node),
    .sel(Reg_Out_Select), .en(and_2_out));  // open: in0, in1, in2, in3, in7
  Multiplexer #(.width(16)) multiplexer_3 (
    .in0(Base_Pointer_q), .in1(undriven_3), .out(multiplexer_3_out), .sel(comparator_1_gt));  // open: en
  Demultiplexer #(.enable("false"), .width(16)) demultiplexer_1 (
    .out0(To_Internal_Data_Bus), .out1(To_Main_Bus), .in(pull_resistor_1_node),
    .sel(REG_Out_to_Mainbus_Select));
  Multiplexer #(.enable("false"), .width(16)) multiplexer_4 (
    .in0(multiplexer_3_out), .in1(stack_pointer_1_data_out), .out(To_Adress_Bus), .sel(Cache_Select));
endmodule

module General_Purpose_Registers (
  input  [15:0] From_Main_Bus,
  input  [15:0] From_Internal_Data_Bus,
  input  Reset,
  input  [31:0] Instruction_Set,
  input  CLK,
  output [15:0] To_Internal_Data_Bus,
  output [15:0] To_Main_Bus
);

  wire comparator_1_eq, comparator_2_eq, comparator_3_eq, comparator_4_eq, comparator_5_eq, comparator_6_eq,
       not_1_out, or_1_out, or_2_out, or_3_out, or_5_out, or_7_out, register_enable_logic_1_out_4,
       register_enable_logic_1_out_5, register_enable_logic_1_out_6, register_enable_logic_1_out_7,
       register_enable_logic_1_out_8, register_enable_logic_1_out_9, register_enable_logic_1_out_10,
       register_enable_logic_1_out_11, xor_1_out;
  wire [1:0] or_4_out;
  wire [2:0] multiplexer_1_out, swap_register_select_1_out_4, swap_register_select_1_out_5;
  wire [7:0] AH_q, AL_q, BH_q, BL_q, CH_q, CL_q, DH_q, DL_q, multiplexer_3_out;
  wire [15:0] multiplexer_2_out, multiplexer_4_out, register_output_logic_1_out_12;

  Comparator #(.mode("unsigned")) comparator_1 (
    .a(Instruction_Set[31:24]), .b(8'h1), .eq(comparator_1_eq));  // open: gt, lt
  Comparator #(.mode("unsigned")) comparator_2 (
    .a(Instruction_Set[31:24]), .b(8'h2), .eq(comparator_2_eq));  // open: gt, lt
  Comparator #(.mode("unsigned")) comparator_3 (
    .a(Instruction_Set[31:24]), .b(8'h3), .eq(comparator_3_eq));  // open: gt, lt
  Comparator #(.mode("unsigned")) comparator_4 (
    .a(Instruction_Set[31:24]), .b(8'h4), .eq(comparator_4_eq));  // open: gt, lt
  Comparator #(.mode("unsigned")) comparator_5 (
    .a(Instruction_Set[31:24]), .b(8'h5), .eq(comparator_5_eq));  // open: gt, lt
  Comparator #(.mode("unsigned")) comparator_6 (
    .a(Instruction_Set[31:24]), .b(8'h20), .eq(comparator_6_eq));  // open: gt, lt
  or or_1 (or_1_out, comparator_4_eq, comparator_3_eq, comparator_6_eq);
  Swap_Register_Select swap_register_select_1 (
    .out_4(swap_register_select_1_out_4), .out_5(swap_register_select_1_out_5),
    .in_1(Instruction_Set[18:16]), .in_2(Instruction_Set[21:19]), .in_3(xor_1_out));
  xor xor_1 (xor_1_out, Instruction_Set[22], or_1_out);
  or or_2 (or_2_out, comparator_3_eq, comparator_4_eq, comparator_6_eq, comparator_2_eq);
  Multiplexer #(.enable("false"), .width(3)) multiplexer_1 (
    .in0(swap_register_select_1_out_5), .in1(swap_register_select_1_out_4), .out(multiplexer_1_out),
    .sel(comparator_6_eq));
  or or_3 (or_3_out, comparator_3_eq, comparator_1_eq, comparator_6_eq, comparator_2_eq, comparator_5_eq);
  or or_4 (or_4_out[0], comparator_6_eq, comparator_2_eq);
  Multiplexer #(.enable("false"), .width(16)) multiplexer_2 (
    .in0(Instruction_Set[15:0]), .in1(multiplexer_4_out), .out(multiplexer_2_out), .sel(or_5_out));
  or or_5 (or_5_out, comparator_6_eq, comparator_2_eq, comparator_3_eq, comparator_5_eq);
  Register_Enable_Logic register_enable_logic_1 (
    .out_4(register_enable_logic_1_out_4), .out_5(register_enable_logic_1_out_5),
    .out_6(register_enable_logic_1_out_6), .out_7(register_enable_logic_1_out_7),
    .out_8(register_enable_logic_1_out_8), .out_9(register_enable_logic_1_out_9),
    .out_10(register_enable_logic_1_out_10), .out_11(register_enable_logic_1_out_11),
    .Register_Activation(or_3_out), .Word_Select(Instruction_Set[23]), .Register_Select(multiplexer_1_out));
  not not_1 (not_1_out, Instruction_Set[23]);
  Multiplexer #(.enable("false"), .width(8)) multiplexer_3 (
    .in0(multiplexer_2_out[15:8]), .in1(multiplexer_2_out[7:0]), .out(multiplexer_3_out), .sel(not_1_out));
  // Probe on AL_q
  Register AL (.D(multiplexer_2_out[7:0]), .en(register_enable_logic_1_out_4), .Q(AL_q), .clk(CLK), .clr(Reset));
  // Probe on BL_q
  Register BL (.D(multiplexer_2_out[7:0]), .en(register_enable_logic_1_out_5), .Q(BL_q), .clk(CLK), .clr(Reset));
  // Probe on CL_q
  Register CL (.D(multiplexer_2_out[7:0]), .en(register_enable_logic_1_out_6), .Q(CL_q), .clk(CLK), .clr(Reset));
  // Probe on DL_q
  Register DL (.D(multiplexer_2_out[7:0]), .en(register_enable_logic_1_out_7), .Q(DL_q), .clk(CLK), .clr(Reset));
  // Probe on AH_q
  Register AH (.D(multiplexer_3_out), .en(register_enable_logic_1_out_8), .Q(AH_q), .clk(CLK), .clr(Reset));
  // Probe on BH_q
  Register BH (.D(multiplexer_3_out), .en(register_enable_logic_1_out_9), .Q(BH_q), .clk(CLK), .clr(Reset));
  // Probe on CH_q
  Register CH (.D(multiplexer_3_out), .en(register_enable_logic_1_out_10), .Q(CH_q), .clk(CLK), .clr(Reset));
  // Probe on DH_q
  Register DH (.D(multiplexer_3_out), .en(register_enable_logic_1_out_11), .Q(DH_q), .clk(CLK), .clr(Reset));
  or or_6 (or_4_out[1], comparator_3_eq, comparator_5_eq);
  Register_Output_Logic register_output_logic_1 (
    .Output_Enable(or_2_out), .Byte_Enable(Instruction_Set[23]),
    .Register_Select(swap_register_select_1_out_4), .AL(AL_q), .BL(BL_q), .CL(CL_q), .DL(DL_q), .AH(AH_q),
    .BH(BH_q), .CH(CH_q), .DH(DH_q), .out_12(register_output_logic_1_out_12));
  Multiplexer #(.enable("false"), .select(2), .width(16)) multiplexer_4 (
    .in0(register_output_logic_1_out_12), .in1(From_Internal_Data_Bus), .in2(From_Main_Bus),
    .out(multiplexer_4_out), .sel(or_4_out));  // open: in3
  or or_7 (or_7_out, comparator_3_eq, comparator_4_eq);
  Demultiplexer #(.enable("false"), .width(16)) demultiplexer_1 (
    .out0(To_Internal_Data_Bus), .out1(To_Main_Bus), .in(register_output_logic_1_out_12), .sel(or_7_out));
endmodule

module Register_Enable_Logic (
  input  [2:0] Register_Select,
  input  Register_Activation,
  input  Word_Select,
  output out_4,
  output out_5,
  output out_6,
  output out_7,
  output out_8,
  output out_9,
  output out_10,
  output out_11
);

  wire and_1_out, decoder_1_out0, decoder_1_out1, decoder_2_out0, decoder_2_out1, decoder_2_out2,
       decoder_2_out3, decoder_3_out0, decoder_3_out1, decoder_3_out2, decoder_3_out3, nand_1_out, or_1_out,
       or_2_out;

  nand nand_1 (nand_1_out, Word_Select, Register_Select[2]);
  Decoder decoder_1 (.out0(decoder_1_out0), .out1(decoder_1_out1), .sel(Register_Select[2]), .en(Register_Activation));
  and and_1 (and_1_out, Register_Activation, Word_Select);
  Pull_Resistor pull_resistor_1 (.node(out_4));
  assign out_4 = nand_1_out ? decoder_2_out0 : 1'bz;  // Controlled_Buffer controlled_buffer_1
  or or_1 (or_1_out, decoder_1_out0, and_1_out);
  or or_2 (or_2_out, and_1_out, decoder_1_out1);
  Decoder #(.select(2)) decoder_2 (
    .out0(decoder_2_out0), .out1(decoder_2_out1), .out2(decoder_2_out2), .out3(decoder_2_out3),
    .sel(Register_Select[1:0]), .en(or_1_out));
  Decoder #(.select(2)) decoder_3 (
    .out0(decoder_3_out0), .out1(decoder_3_out1), .out2(decoder_3_out2), .out3(decoder_3_out3),
    .sel(Register_Select[1:0]), .en(or_2_out));
  Pull_Resistor pull_resistor_2 (.node(out_5));
  Pull_Resistor pull_resistor_3 (.node(out_6));
  Pull_Resistor pull_resistor_4 (.node(out_7));
  Pull_Resistor pull_resistor_5 (.node(out_8));
  assign out_5 = nand_1_out ? decoder_2_out1 : 1'bz;  // Controlled_Buffer controlled_buffer_2
  assign out_6 = nand_1_out ? decoder_2_out2 : 1'bz;  // Controlled_Buffer controlled_buffer_3
  assign out_7 = nand_1_out ? decoder_2_out3 : 1'bz;  // Controlled_Buffer controlled_buffer_4
  assign out_8 = nand_1_out ? decoder_3_out0 : 1'bz;  // Controlled_Buffer controlled_buffer_5
  Pull_Resistor pull_resistor_6 (.node(out_9));
  Pull_Resistor pull_resistor_7 (.node(out_10));
  Pull_Resistor pull_resistor_8 (.node(out_11));
  assign out_9 = nand_1_out ? decoder_3_out1 : 1'bz;  // Controlled_Buffer controlled_buffer_6
  assign out_10 = nand_1_out ? decoder_3_out2 : 1'bz;  // Controlled_Buffer controlled_buffer_7
  assign out_11 = nand_1_out ? decoder_3_out3 : 1'bz;  // Controlled_Buffer controlled_buffer_8
endmodule

module Register_Output_Logic (
  input  Output_Enable,
  input  Byte_Enable,
  input  [2:0] Register_Select,
  input  [7:0] AL,
  input  [7:0] BL,
  input  [7:0] CL,
  input  [7:0] DL,
  input  [7:0] AH,
  input  [7:0] BH,
  input  [7:0] CH,
  input  [7:0] DH,
  output [15:0] out_12
);

  wire and_1_out, and_2_out, and_3_out, not_1_out, one_bit_narrow_and_1_o, one_bit_narrow_or_1_o,
       one_bit_narrow_or_2_o, pull_resistor_1_node;
  wire [7:0] multiplexer_1_out, multiplexer_2_out, multiplexer_3_out, pull_resistor_2_node;

  not not_1 (not_1_out, Byte_Enable);
  Pull_Resistor pull_resistor_1 (.node(pull_resistor_1_node));
  assign pull_resistor_1_node = not_1_out ? Register_Select[2] : 1'bz;  // Controlled_Buffer controlled_buffer_1
  and and_1 (and_1_out, ~Byte_Enable, ~Register_Select[2]);  // AND_Gate
  and and_2 (and_2_out, ~Byte_Enable, Register_Select[2]);  // AND_Gate
  One_Bit_Narrow_OR one_bit_narrow_or_1 (.O(one_bit_narrow_or_1_o), .A(Byte_Enable), .B(and_1_out));
  Multiplexer #(.enable("false"), .width(8)) multiplexer_1 (
    .in0(multiplexer_2_out), .in1(multiplexer_3_out), .out(multiplexer_1_out), .sel(pull_resistor_1_node));
  Multiplexer #(.select(2), .width(8)) multiplexer_2 (
    .in0(AL), .in1(BL), .in2(CL), .in3(DL), .out(multiplexer_2_out), .sel(Register_Select[1:0]),
    .en(one_bit_narrow_or_1_o));
  One_Bit_Narrow_AND one_bit_narrow_and_1 (.O(one_bit_narrow_and_1_o), .A(Register_Select[2]), .B(Byte_Enable));
  Pull_Resistor pull_resistor_2 (.node(pull_resistor_2_node));
  assign pull_resistor_2_node = Byte_Enable ? multiplexer_3_out : 8'bz;  // Controlled_Buffer controlled_buffer_2
  Multiplexer #(.select(2), .width(8)) multiplexer_3 (
    .in0(AH), .in1(BH), .in2(CH), .in3(DH), .out(multiplexer_3_out), .sel(Register_Select[1:0]),
    .en(one_bit_narrow_or_2_o));
  One_Bit_Narrow_OR one_bit_narrow_or_2 (.O(one_bit_narrow_or_2_o), .A(Byte_Enable), .B(and_2_out));
  and and_3 (and_3_out, Output_Enable, ~one_bit_narrow_and_1_o);  // AND_Gate
  Pull_Resistor pull_resistor_3 (.node(out_12));
  assign out_12 = and_3_out ? {pull_resistor_2_node, multiplexer_1_out} : 16'bz;  // Controlled_Buffer controlled_buffer_3
endmodule

module Swap_Register_Select (
  input  [2:0] in_1,
  input  [2:0] in_2,
  input  in_3,
  output [2:0] out_4,
  output [2:0] out_5
);

  Multiplexer #(.enable("false"), .width(3)) multiplexer_1 (.in0(in_2), .in1(in_1), .out(out_4), .sel(in_3));
  Multiplexer #(.enable("false"), .width(3)) multiplexer_2 (.in0(in_1), .in1(in_2), .out(out_5), .sel(in_3));
endmodule

module Instruction_Decoder (
  input  [31:0] Instruction_Set,
  output Read_Data_from_Memory,
  output Write_Data_to_Memory,
  output Use_Cache,
  output Word_Select,
  output REG_Enable,
  output [2:0] REG_Select,
  output [1:0] Register_in_Select,
  output Reg_Out_Enable,
  output [2:0] Reg_Out_Select,
  output Cache_Select,
  output REG_Out_to_Mainbus_Select
);

  wire and_1_out, and_2_out, comparator_3_eq, comparator_4_eq, comparator_5_eq, not_1_out,
       one_bit_narrow_and_1_o;

  Comparator comparator_1 (.a(Instruction_Set[31:24]), .b(8'h1), .eq(REG_Enable));  // open: gt, lt
  One_Bit_Narrow_AND one_bit_narrow_and_1 (.O(one_bit_narrow_and_1_o), .A(REG_Enable), .B(Instruction_Set[22]));
  Comparator comparator_2 (.a(Instruction_Set[31:24]), .b(8'h2));  // open: gt, eq, lt
  Comparator comparator_3 (.a(Instruction_Set[31:24]), .b(8'h3), .eq(comparator_3_eq));  // open: gt, lt
  Comparator comparator_4 (.a(Instruction_Set[31:24]), .b(8'h4), .eq(comparator_4_eq));  // open: gt, lt
  Comparator comparator_5 (.a(Instruction_Set[31:24]), .b(8'h5), .eq(comparator_5_eq));  // open: gt, lt
  Multiplexer #(.enable("false"), .width(3)) multiplexer_1 (
    .in0(Instruction_Set[18:16]), .in1(Instruction_Set[21:19]), .out(REG_Select), .sel(one_bit_narrow_and_1_o));
  and and_1 (and_1_out, Instruction_Set[22], comparator_3_eq);
  not not_1 (not_1_out, Instruction_Set[22]);
  and and_2 (and_2_out, not_1_out, comparator_3_eq);
  or or_1 (Read_Data_from_Memory, and_1_out, comparator_5_eq);
  or or_2 (Write_Data_to_Memory, and_2_out, comparator_4_eq);
  or or_3 (Use_Cache, comparator_4_eq, comparator_5_eq);

  assign Word_Select = Instruction_Set[23];
endmodule

module One_Bit_Narrow_AND (
  input  A,
  input  B,
  output O
);

  and and_1 (O, A, B);
endmodule

module One_Bit_Narrow_OR (
  input  A,
  input  B,
  output O
);

  or or_1 (O, A, B);
endmodule

module Stack_Pointer (
  input  Up_Down,
  input  Load_Data,
  input  [15:0] Data_IN,
  input  Enable,
  input  POP,
  input  CLK,
  input  RESET,
  output [15:0] Data_OUT
);

  wire [15:0] Stack_Pointer_q, subtractor_1_out;

  Counter #(.max('hffff), .trigger("falling"), .width(16)) Stack_Pointer (
    .load(Load_Data), .D(Data_IN), .count(Enable), .Q(Stack_Pointer_q), .up(Up_Down), .clk(CLK), .clr(RESET));  // open: carry
  Subtractor #(.width(16)) subtractor_1 (.a(Stack_Pointer_q), .b(16'h1), .out(subtractor_1_out));  // open: bin, bout
  Multiplexer #(.enable("false"), .width(16)) multiplexer_1 (
    .in0(Stack_Pointer_q), .in1(subtractor_1_out), .out(Data_OUT), .sel(POP));
endmodule

module ALU (
  input  [15:0] From_Internal_Bus,
  input  [31:0] Instruction_Set,
  input  CLK,
  output [15:0] To_Internal_Bus
);

  wire adder_1_cout, comparator_1_eq;
  wire [0:0] pull_resistor_1_node;
  wire [15:0] adder_1_out, controlled_buffer_1_out, or_2_out, register_1_q;

  Comparator comparator_1 (.a(Instruction_Set[31:24]), .b(8'h20), .eq(comparator_1_eq));  // open: gt, lt
  assign controlled_buffer_1_out = comparator_1_eq ? adder_1_out : 16'bz;  // Controlled_Buffer controlled_buffer_1
  Adder #(.width(16)) adder_1 (
    .a(From_Internal_Bus), .b(Instruction_Set[15:0]), .out(adder_1_out), .cout(adder_1_cout));  // open: cin
  Pull_Resistor pull_resistor_1 (.node(pull_resistor_1_node[0]));
  assign pull_resistor_1_node[0] = comparator_1_eq ? adder_1_cout : 1'bz;  // Controlled_Buffer controlled_buffer_2
  Pull_Resistor pull_resistor_2 (.node(To_Internal_Bus));
  assign To_Internal_Bus = controlled_buffer_1_out;  // OR_Gate or_1, 16 bits wide OR_Gate
  assign or_2_out = register_1_q | {{15{1'b0}}, pull_resistor_1_node[0]};  // OR_Gate or_2, 16 bits wide
  // Probe on register_1_q
  Register #(.width(16)) register_1 (.D(or_2_out), .Q(register_1_q), .clk(CLK));  // open: en, clr
endmodule
